// Logisim project atividade_26_08_22.circ as structural Verilog: 1 circuit, main circuit main
module main (
  input  in_1,
  input  in_2
);

  wire and_1_out, and_2_out, and_3_out, and_4_out, and_5_out, and_6_out, and_7_out, and_8_out, clock_1_out,
       clock_2_out, clock_3_out, clock_4_out, not_1_out, not_2_out, or_1_out;

  Clock clock_1 (.out(clock_1_out));
  Clock clock_2 (.out(clock_2_out));
  Clock clock_3 (.out(clock_3_out));
  Clock clock_4 (.out(clock_4_out));
  and and_1 (and_1_out, ~in_1, ~in_2, clock_1_out);  // AND_Gate
  and and_2 (and_2_out, ~in_1, in_2, clock_2_out);  // AND_Gate
  and and_3 (and_3_out, in_1, ~in_2, clock_3_out);  // AND_Gate
  and and_4 (and_4_out, in_1, in_2, clock_4_out);
  or or_1 (or_1_out, and_1_out, and_2_out, and_3_out, and_4_out);
  not not_1 (not_1_out, in_1);
  not not_2 (not_2_out, in_2);
  and and_5 (and_5_out, not_1_out, not_2_out, or_1_out);
  LED led_1 (.in(and_5_out));
  and and_6 (and_6_out, not_1_out, in_2, or_1_out);
  LED led_2 (.in(and_6_out));
  and and_7 (and_7_out, in_1, not_2_out, or_1_out);
  LED led_3 (.in(and_7_out));
  LED led_4 (.in(and_8_out));
  and and_8 (and_8_out, in_1, in_2, or_1_out);
endmodule
