// Logisim project atividade_26_08_22_8entrada.circ as structural Verilog: 1 circuit, main circuit main
module main (
  input  A,
  input  B,
  input  C
);

  wire and_1_out, and_2_out, and_3_out, and_4_out, and_5_out, and_6_out, and_7_out, and_8_out, and_9_out,
       and_10_out, and_11_out, and_12_out, and_13_out, and_16_out, and_17_out, and_18_out, and_19_out,
       and_20_out, and_21_out, and_22_out, and_23_out, and_24_out, clock_1_out, clock_2_out, clock_3_out,
       clock_4_out, clock_5_out, clock_6_out, clock_7_out, clock_8_out, or_1_out, or_2_out, or_3_out;

  Clock clock_1 (.out(clock_1_out));
  Clock clock_2 (.out(clock_2_out));
  Clock clock_3 (.out(clock_3_out));
  Clock clock_4 (.out(clock_4_out));
  Clock clock_5 (.out(clock_5_out));
  Clock clock_6 (.out(clock_6_out));
  Clock clock_7 (.out(clock_7_out));
  Clock clock_8 (.out(clock_8_out));
  and and_1 (and_1_out, ~A, ~B, clock_1_out);  // AND_Gate
  and and_2 (and_2_out, ~A, B, clock_2_out);  // AND_Gate
  and and_3 (and_3_out, A, ~B, clock_3_out);  // AND_Gate
  and and_4 (and_4_out, A, B, clock_4_out);
  and and_5 (and_5_out, ~A, ~B, clock_5_out);  // AND_Gate
  and and_6 (and_6_out, ~A, B, clock_6_out);  // AND_Gate
  and and_7 (and_7_out, A, ~B, clock_7_out);  // AND_Gate
  and and_8 (and_8_out, A, B, clock_8_out);
  or or_1 (or_1_out, and_1_out, and_2_out, and_3_out, and_4_out);
  or or_2 (or_2_out, and_5_out, and_6_out, and_7_out, and_8_out);
  and and_9 (and_9_out, ~C, ~C, or_1_out);  // AND_Gate
  and and_10 (and_10_out, ~C, C);  // AND_Gate
  and and_11 (and_11_out, C, ~C);  // AND_Gate
  and and_12 (and_12_out, C, C, or_2_out);
  or or_3 (or_3_out, and_9_out, and_10_out, and_11_out, and_12_out);
  and and_13 (and_13_out, ~B, ~B, or_3_out);  // AND_Gate
  // AND_Gate and_14 has open pins: in0=B, in1=B, in2=or_3_out, out=open
  // AND_Gate and_15 has open pins: in0=B, in1=B, in2=or_3_out, out=open
  and and_16 (and_16_out, B, B, or_3_out);
  and and_17 (and_17_out, ~A, ~C, and_13_out);  // AND_Gate
  and and_18 (and_18_out, ~A, C, and_13_out);  // AND_Gate
  and and_19 (and_19_out, A, ~C, and_13_out);  // AND_Gate
  and and_20 (and_20_out, A, C, and_13_out);
  and and_21 (and_21_out, ~A, ~C, and_16_out);  // AND_Gate
  and and_22 (and_22_out, ~A, C, and_16_out);  // AND_Gate
  and and_23 (and_23_out, A, ~C, and_16_out);  // AND_Gate
  and and_24 (and_24_out, A, C, and_16_out);
  LED led_1 (.in(and_17_out));
  LED led_2 (.in(and_18_out));
  LED led_3 (.in(and_19_out));
  LED led_4 (.in(and_20_out));
  LED led_5 (.in(and_21_out));
  LED led_6 (.in(and_22_out));
  LED led_7 (.in(and_23_out));
  LED led_8 (.in(and_24_out));
endmodule
